# Fritzing sketch esp32 (saved by Fritzing 0.9.3b)

parts:
  Mod1 = ESP32-TTGO-T-DISPLAY
  Onderdeel1 = NRF24L01+ Breakout Board

nets:
  N1: Mod1.G-1, Mod1.G-14, Onderdeel1.GND
  N2: Mod1.21, Onderdeel1.MISO
  N3: Mod1.22, Onderdeel1.SCK
  N4: Mod1.17, Onderdeel1.CE
  N5: Mod1.15, Onderdeel1.CS
  N6: Mod1.13, Onderdeel1.MOSI
  N7: Mod1.3V, Onderdeel1.VCC
  N8: Mod1.36, Onderdeel1.IRQ

custom parts:
  ESP32-TTGO-T-DISPLAY: LILYGO TTGO T-Display GD32VF103CBT6 Main Chip ST7789 1.14 Inch IPS 240x135 Resolution Minimalist Development Board.
