# Fritzing sketch esp8266 (saved by Fritzing 0.9.3b)

parts:
  WeMos_D1_R1 = WeMos D1 R2
  Onderdeel1 = NRF24L01+ Breakout Board

nets:
  N1: WeMos_D1_R1.D3, Onderdeel1.CS
  N2: WeMos_D1_R1.D4, Onderdeel1.CE
  N3: WeMos_D1_R1.D11, Onderdeel1.MOSI
  N4: WeMos_D1_R1.D12, Onderdeel1.MISO
  N5: WeMos_D1_R1.D13, Onderdeel1.SCK
  N6: WeMos_D1_R1.D15, Onderdeel1.IRQ
  GND: WeMos_D1_R1.GND, Onderdeel1.GND
  3.3V: WeMos_D1_R1.3.3V, Onderdeel1.VCC

custom parts:
  WeMos D1 R2: The D1 R2 is a mini wifi board based on the ESP-8266EX.
