# Fritzing sketch uno (saved by Fritzing 0.9.3b)

parts:
  Onderdeel2 = NRF24L01+ Breakout Board
  Onderdeel1 = Arduino Uno (Rev3)

nets:
  GND: Onderdeel2.GND, Onderdeel1.GND
  VCC: Onderdeel2.VCC, Onderdeel1.3V3
  N1: Onderdeel2.CE, Onderdeel1.D8
  N2: Onderdeel2.CS, Onderdeel1.D7
  N3: Onderdeel2.SCK, Onderdeel1.D13/SCK
  N4: Onderdeel2.MOSI, Onderdeel1.D11_PWM/MOSI
  N5: Onderdeel2.MISO, Onderdeel1.D12/MISO
  N6: Onderdeel2.IRQ, Onderdeel1.D2
